# Fritzing sketch _BOARD_NANO (saved by Fritzing 0.9.3b)
circuit board: 8.46667cm x 5.64444cm
breadboards: 1

parts:
  Bauteil1 = Arduino Nano (Rev3.0) [part_number="Arduino Nano V3.0"]
  ZS-042_RTC1 = ZS-042 RTC Module [part_number="DS3231 RTC Modul"]  # not connected
  S8 = Pushbutton [part_number=Minute+ package="[THT]"]
  S10 = Pushbutton [part_number=Hour+ package="[THT]"]
  LED2 = LED - 3mm [color="Yellow (595nm)" part_number="DCF77 LED" package="3 mm [THT]"]
  R5 = Resistor [tolerance=±5% resistance=1k package=THT]
  R6 = Photocell (LDR) [part_number="LDR A9013" package=THT]
  J2 = female pin header, 4 pins [form="♀ (female)" part_number="DCF77 Header 3V3, GND, DATA, PON"]
  T1 = LM35 Temperature Sensor [part_number="Temperature Sensor LM35" package="TO92 [THT]"]
  J1 = female pin header, 4 pins [form="♀ (female)" part_number="LED-Stripe Header 5V, GND, DATA, (CLOCK)"]
  IR1 = TSOP312.., 314.. [part_number="IR Receiver TSOP31240" package=THT]
  R8 = Resistor [tolerance=±5% resistance=10k package=THT]
  R9 = Resistor [tolerance=±5% resistance=10k package=THT]
  R2 = Resistor [tolerance=±5% resistance=10k package=THT]
  S11 = Pushbutton [part_number=Mode package="[THT]"]
  R11 = Resistor [tolerance=±5% resistance=10k package=THT]
  J3 = Piezo Speaker

nets:
  GND: Bauteil1.GND, S8.Pin_3, S8.Pin_4, S10.Pin_3, S10.Pin_4, R5.Pin_1, R6.pin_1, J2.pin3, T1.GND, J1.pin3, IR1.GND, S11.Pin_3, S11.Pin_4, J3.pin1
  N1: Bauteil1.D3, J2.pin2
  N2: Bauteil1.D4, J2.pin1
  N3: Bauteil1.D5, J1.pin2
  N4: Bauteil1.D6, J1.pin1
  N5: Bauteil1.D8, S8.Pin_1, S8.Pin_2, R11.Pin_0
  N6: Bauteil1.D9, S10.Pin_1, S10.Pin_2, R2.Pin_0
  N7: Bauteil1.D10, R9.Pin_0, S11.Pin_1, S11.Pin_2
  N8: Bauteil1.D11/MOSI, J3.pin2
  N9: Bauteil1.D12/MISO, LED2.anode
  N10: Bauteil1.5V, T1.+Vs, J1.pin4, IR1.Vs
  N11: Bauteil1.A2, T1.Vout
  N12: Bauteil1.A1, IR1.Data
  N13: Bauteil1.A0, R6.pin_0, R8.Pin_0
  N14: Bauteil1.3V3, J2.pin4

notes:
  BOARD_NANO
  DCF77 Header (left):
  3V3, GND, DATA, PON
  LED-Stripe Header (right):
  5V, GND, (CLOCK), DATA
